// Logisim project Logic.circ as structural Verilog: 5 circuits, main circuit Main
// DECODER
module _8bitDecoder (
  input  P1,
  input  P2,
  input  P3,
  output out_4,
  output out_5,
  output out_6,
  output out_7,
  output out_8,
  output out_9,
  output out_10,
  output out_11
);

  wire and_1_out, and_2_out, and_3_out, and_4_out, not_1_out, not_2_out, not_3_out;

  not not_1 (not_1_out, P2);
  not not_2 (not_2_out, P1);
  and and_1 (and_1_out, not_2_out, not_1_out);
  and and_2 (and_2_out, not_2_out, P2);
  and and_3 (and_3_out, not_1_out, P1);
  and and_4 (and_4_out, P1, P2);
  not not_3 (not_3_out, P3);
  and _0 (out_4, and_1_out, not_3_out);
  and _1 (out_5, and_1_out, P3);
  and _2 (out_6, and_2_out, not_3_out);
  and _3 (out_7, and_2_out, P3);
  and _4 (out_8, and_3_out, not_3_out);
  and _5 (out_9, and_3_out, P3);
  and _6 (out_10, and_4_out, not_3_out);
  and _7 (out_11, and_4_out, P3);

  // Notes on the sheet:
  //   P Decoder
  //   ANUJ KHURANA -- S5281041
endmodule

// DECODER
module QDecoder (
  input  Q1,
  input  Q2,
  input  Q3,
  output out_4,
  output out_5,
  output out_6,
  output out_7,
  output out_8,
  output out_9,
  output out_10,
  output out_11
);

  wire and_1_out, and_2_out, and_3_out, and_4_out, not_1_out, not_2_out, not_3_out;

  not not_1 (not_1_out, Q1);
  not not_2 (not_2_out, Q2);
  and and_1 (and_1_out, not_1_out, not_2_out);
  and and_2 (and_2_out, not_1_out, Q2);
  and and_3 (and_3_out, not_2_out, Q1);
  and and_4 (and_4_out, Q1, Q2);
  not not_3 (not_3_out, Q3);
  and _0 (out_4, and_1_out, not_3_out);
  and _1 (out_5, and_1_out, Q3);
  and _2 (out_6, and_2_out, not_3_out);
  and _3 (out_7, and_2_out, Q3);
  and _4 (out_8, and_3_out, not_3_out);
  and _5 (out_9, and_3_out, Q3);
  and _6 (out_10, and_4_out, not_3_out);
  and _7 (out_11, and_4_out, Q3);

  // Notes on the sheet:
  //   Q Decoder
  //   ANUJ KHURANA -- S5281041
endmodule

module logic_P_Q (
  input  P0,
  input  P1,
  input  P2,
  input  P3,
  input  P4,
  input  P5,
  input  P6,
  input  P7,
  input  Q0,
  input  Q1,
  input  Q2,
  input  Q3,
  input  Q4,
  input  Q5,
  input  Q6,
  input  Q7,
  output OUTPUT_P_Q
);

  wire _0_1_out, _0_2_3_out, _0_out, _1_2_out, _1_out, _2_3_out, _2_out, _3_4_out, _3_out, _4_5_7_out,
       _4_5_out, _4_out, _5_6_out, _5_out, _6_7_out, _6_out, _7_out, _0134_out, _1245_out, _2356_out,
       _3467_out, or_1_out, or_2_out, or_3_out, or_4_out, or_5_out, or_6_out;

  or _0_1 (_0_1_out, Q0, Q1);
  or _1_2 (_1_2_out, Q1, Q2);
  or _2_3 (_2_3_out, Q2, Q3);
  or _3_4 (_3_4_out, Q3, Q4);
  or _4_5 (_4_5_out, Q4, Q5);
  or _5_6 (_5_6_out, Q5, Q6);
  or _6_7 (_6_7_out, Q6, Q7);
  or _0_2_3 (_0_2_3_out, Q0, _2_3_out);
  or _0134 (_0134_out, _0_1_out, _3_4_out);
  or _1245 (_1245_out, _1_2_out, _4_5_out);
  or _2356 (_2356_out, _2_3_out, _5_6_out);
  or _3467 (_3467_out, _3_4_out, _6_7_out);
  or _4_5_7 (_4_5_7_out, _4_5_out, Q7);
  and _0 (_0_out, P0, _1_2_out);
  and _1 (_1_out, P1, _0_2_3_out);
  and _2 (_2_out, P2, _0134_out);
  and _3 (_3_out, P3, _1245_out);
  and _4 (_4_out, P4, _2356_out);
  and _5 (_5_out, P5, _3467_out);
  and _6 (_6_out, P6, _4_5_7_out);
  and _7 (_7_out, P7, _5_6_out);
  or or_1 (or_1_out, _0_out, _1_out);
  or or_2 (or_2_out, _2_out, _3_out);
  or or_3 (or_3_out, _4_out, _5_out);
  or or_4 (or_4_out, _6_out, _7_out);
  or or_5 (or_5_out, or_1_out, or_2_out);
  or or_6 (or_6_out, or_3_out, or_4_out);
  or or_7 (OUTPUT_P_Q, or_5_out, or_6_out);

  // Notes on the sheet:
  //   P = Q + 2
  //   ANUJ KHURANA -- S5281041
  //   P = Q - 2
  //   P = Q + 1
  //   P = Q - 1
endmodule

module PART_B (
  input  in_1,
  input  Button,
  output out_3
);

  wire comparator_1_eq, comparator_2_eq, not_1_out;
  wire [2:0] counter_1_q, counter_2_q;

  Counter #(.width(3), .max('h4), .ongoal("stay")) counter_1 (
    .count(not_1_out), .Q(counter_1_q), .clk(Button), .clr(comparator_1_eq));  // open: load, D, carry
  not not_1 (not_1_out, in_1);
  Counter #(.width(3), .max('h6), .ongoal("stay")) counter_2 (
    .count(in_1), .Q(counter_2_q), .clk(Button), .clr(comparator_1_eq));  // open: load, D, carry
  Comparator #(.width(3), .mode("unsigned")) comparator_1 (
    .a(3'b011), .b(counter_1_q), .eq(comparator_1_eq));  // open: gt, lt
  Comparator #(.width(3), .mode("unsigned")) comparator_2 (
    .a(3'b110), .b(counter_2_q), .eq(comparator_2_eq));  // open: gt, lt
  D_Flip_Flop d_ff_1 (.Q(out_3), .preset(comparator_2_eq));  // open: clk, D, Qn, en, reset

  // Notes on the sheet:
  //   PART B LOGIC
  //   Unsuccessful
  //   3 Unsuccessful = reset
  //   Successful
  //   6 successful = stop
  //   counter
  //   ANUJ KHURANA -- S5281041
  //   comparator
  //   comparator
  //   Dflipflop
  //   SIMULATION STOPPED
endmodule

module Main (
  input  in_1,
  input  in_2,
  input  in_3,
  input  in_4,
  input  in_5,
  input  in_6,
  output out_7
);

  wire button_1_out, logic_p_q_1_output_p_q, n8bitdecoder_1_out_4, n8bitdecoder_1_out_5,
       n8bitdecoder_1_out_6, n8bitdecoder_1_out_7, n8bitdecoder_1_out_8, n8bitdecoder_1_out_9,
       n8bitdecoder_1_out_10, n8bitdecoder_1_out_11, qdecoder_1_out_4, qdecoder_1_out_5, qdecoder_1_out_6,
       qdecoder_1_out_7, qdecoder_1_out_8, qdecoder_1_out_9, qdecoder_1_out_10, qdecoder_1_out_11;

  Button button_1 (.out(button_1_out));
  _8bitDecoder u_8bitdecoder_1 (
    .out_4(n8bitdecoder_1_out_4), .out_5(n8bitdecoder_1_out_5), .out_6(n8bitdecoder_1_out_6),
    .out_7(n8bitdecoder_1_out_7), .out_8(n8bitdecoder_1_out_8), .P1(in_1), .out_9(n8bitdecoder_1_out_9),
    .P2(in_2), .out_10(n8bitdecoder_1_out_10), .out_11(n8bitdecoder_1_out_11), .P3(in_3));
  QDecoder qdecoder_1 (
    .Q1(in_4), .Q2(in_5), .Q3(in_6), .out_4(qdecoder_1_out_4), .out_5(qdecoder_1_out_5),
    .out_6(qdecoder_1_out_6), .out_7(qdecoder_1_out_7), .out_8(qdecoder_1_out_8), .out_9(qdecoder_1_out_9),
    .out_10(qdecoder_1_out_10), .out_11(qdecoder_1_out_11));
  logic_P_Q logic_p_q_1 (
    .Q0(qdecoder_1_out_4), .Q1(qdecoder_1_out_5), .Q2(qdecoder_1_out_6), .Q3(qdecoder_1_out_7),
    .Q4(qdecoder_1_out_8), .Q5(qdecoder_1_out_9), .Q6(qdecoder_1_out_10), .Q7(qdecoder_1_out_11),
    .P2(n8bitdecoder_1_out_6), .P3(n8bitdecoder_1_out_7), .P4(n8bitdecoder_1_out_8),
    .P5(n8bitdecoder_1_out_9), .P6(n8bitdecoder_1_out_10), .P7(n8bitdecoder_1_out_11),
    .P1(n8bitdecoder_1_out_5), .P0(n8bitdecoder_1_out_4), .OUTPUT_P_Q(logic_p_q_1_output_p_q));
  PART_B part_b_1 (.in_1(logic_p_q_1_output_p_q), .out_3(out_7), .Button(button_1_out));

  // Notes on the sheet:
  //   Count Button
  //   ANUJ KHURANA -- S5281041
  //   P
  //   Q
  //   SIMULATION STOPPED
endmodule
